// Logisim project Z23 - Simon.circ as structural Verilog: 7 circuits, main circuit main
module main (
  output [7:0] OUT
);

  wire and_1_out, clock_1_out, control_1_halt, control_1_imty, control_1_mw, control_1_rsource, control_1_rw,
       decoder_1_rd, decoder_1_rs;
  wire [2:0] decoder_1_func, decoder_1_opc;
  wire [5:0] decoder_1_addr;
  wire [7:0] decoder_1_imm, memory_1_out, multiplexer_1_out, multiplexer_2_out, register_file_1_r_rd,
       register_file_1_r_rs;
  wire [15:0] instr_memory_1_cir;

  memory memory_1 (
    .ADDR(decoder_1_addr), .MW(control_1_mw), .IN(register_file_1_r_rd), .OUT(memory_1_out), .clk(and_1_out));
  Multiplexer #(.width(8), .enable("false")) multiplexer_1 (
    .in0(OUT), .in1(memory_1_out), .out(multiplexer_1_out), .sel(control_1_rsource));
  register_file register_file_1 (
    .rd(decoder_1_rd), .rs(decoder_1_rs), .RW(control_1_rw), .clk(and_1_out), .IN(multiplexer_1_out),
    .R_rs(register_file_1_r_rs), .R_rd(register_file_1_r_rd));
  Multiplexer #(.width(8), .enable("false")) multiplexer_2 (
    .in0(register_file_1_r_rd), .in1(decoder_1_imm), .out(multiplexer_2_out), .sel(control_1_imty));
  and and_1 (and_1_out, clock_1_out, ~control_1_halt);  // AND_Gate
  ALU alu_1 (.OUT(OUT), .func(decoder_1_func), .A(register_file_1_r_rs), .B(multiplexer_2_out));
  Clock clock_1 (.out(clock_1_out));
  instr_memory instr_memory_1 (.clk(and_1_out), .CIR(instr_memory_1_cir));
  decoder decoder_1 (
    .CIR(instr_memory_1_cir), .addr(decoder_1_addr), .imm(decoder_1_imm), .func(decoder_1_func),
    .rs(decoder_1_rs), .rd(decoder_1_rd), .opc(decoder_1_opc));
  control control_1 (
    .MW(control_1_mw), .Rsource(control_1_rsource), .RW(control_1_rw), .imty(control_1_imty),
    .halt(control_1_halt), .OPC(decoder_1_opc));
endmodule

// REG_FILE
module register_file (
  input  [7:0] IN,
  input  clk,
  input  rd,
  input  rs,
  input  RW,
  output [7:0] R_rs,
  output [7:0] R_rd
);

  wire and_1_out, and_2_out;
  wire [7:0] r0_q, r1_q;

  and and_1 (and_1_out, ~rd, RW);  // AND_Gate
  and and_2 (and_2_out, rd, RW);
  Register r0 (.D(IN), .en(and_1_out), .Q(r0_q), .clk(clk));  // open: clr
  Register r1 (.D(IN), .en(and_2_out), .Q(r1_q), .clk(clk));  // open: clr
  Multiplexer #(.width(8), .enable("false")) multiplexer_1 (.in0(r0_q), .in1(r1_q), .out(R_rd), .sel(rd));
  Multiplexer #(.width(8), .enable("false")) multiplexer_2 (.in0(r0_q), .in1(r1_q), .out(R_rs), .sel(rs));
endmodule

module decoder (
  input  [15:0] CIR,
  output [5:0] addr,
  output [7:0] imm,
  output [2:0] func,
  output rs,
  output rd,
  output [2:0] opc
);


  assign addr = CIR[5:0];
  assign func = CIR[10:8];
  assign imm = CIR[7:0];
  assign opc = CIR[15:13];
  assign rd = CIR[12];
  assign rs = CIR[11];
endmodule

// mem
module memory (
  input  [7:0] IN,
  input  [5:0] ADDR,
  input  MW,
  input  clk,
  output [7:0] OUT
);

  RAM #(.addrWidth(6), .bus("separate")) ram_1 (
    .addr(ADDR), .din(IN), .data(OUT), .str(MW), .clk(clk));  // open: sel, ld, clr
endmodule

// control_unit
module control (
  input  [2:0] OPC,
  output MW,
  output Rsource,
  output RW,
  output imty,
  output halt
);

  wire and_2_out, and_3_out, and_5_out, multiplexer_1_out, not_1_out, not_2_out, not_4_out, not_5_out;

  not not_1 (not_1_out, OPC[2]);
  not not_2 (not_2_out, OPC[2]);
  not not_3 (imty, OPC[1]);
  not not_4 (not_4_out, OPC[1]);
  not not_5 (not_5_out, OPC[0]);
  and and_1 (Rsource, OPC[1], OPC[0]);
  and and_2 (and_2_out, not_1_out, OPC[0]);
  or or_1 (RW, and_2_out, and_3_out);
  and and_3 (and_3_out, not_2_out, OPC[1]);
  and and_4 (MW, not_4_out, not_5_out);
  and and_5 (and_5_out, RW, imty, MW);
  Multiplexer #(.enable("false")) multiplexer_1 (.in0(Rsource), .in1(and_5_out), .out(multiplexer_1_out), .sel(RW));
  Comparator #(.width(1)) comparator_1 (.a(multiplexer_1_out), .b(1'b1), .eq(halt));  // open: gt, lt
endmodule

module ALU (
  input  [7:0] A,
  input  [7:0] B,
  input  [2:0] func,
  output [7:0] OUT
);

  wire comparator_1_lt;
  wire [7:0] adder_1_out, divider_1_out, divider_1_rem, multiplexer_1_out, multiplier_1_out, subtractor_1_out;

  Adder adder_1 (.a(A), .b(B), .out(adder_1_out));  // open: cin, cout
  Subtractor subtractor_1 (.a(A), .b(B), .out(subtractor_1_out));  // open: bin, bout
  Multiplier multiplier_1 (.a(A), .b(B), .out(multiplier_1_out));  // open: cin, cout
  Divider divider_1 (.a(A), .b(B), .out(divider_1_out), .rem(divider_1_rem));  // open: upper
  Comparator comparator_1 (.a(A), .b(B), .lt(comparator_1_lt));  // open: gt, eq
  Multiplexer #(.width(8), .enable("false")) multiplexer_1 (
    .in0(B), .in1(A), .out(multiplexer_1_out), .sel(comparator_1_lt));
  Multiplexer #(.select(3), .width(8), .enable("false")) multiplexer_2 (
    .in0(A), .in1(B), .in2(adder_1_out), .in3(subtractor_1_out), .in4(multiplier_1_out), .in5(divider_1_out),
    .in6(divider_1_rem), .in7(multiplexer_1_out), .out(OUT), .sel(func));
endmodule

// instr\nmem
module instr_memory (
  input  clk,
  output [15:0] CIR
);

  wire [5:0] counter_1_q;

  Counter #(.width(6), .max('h3f)) counter_1 (.Q(counter_1_q), .clk(clk));  // open: load, D, count, carry, clr
  RAM #(.addrWidth(6), .dataWidth(16)) ram_1 (.addr(counter_1_q), .data(CIR), .clk(clk));  // open: sel, ld, clr
endmodule
