// Logisim project Z23 (1).circ as structural Verilog: 13 circuits, main circuit Z23
module Z23 (
  input  PC_____0,
  output HALT
);

  wire CLK, IMTY, multiplexer_3_out, MW, not_1_out, RD, RS, RSource, RW;
  wire [2:0] Decoder_opc, FUNC;
  wire [5:0] ADDR;
  wire [7:0] ALU_output_alu, Data_Mem_read_data, IMM, multiplexer_1_out, multiplexer_2_out, Registers_rd_2,
       Registers_rs_2;
  wire [15:0] Instr_Mem_out_2;

  // Probe on ALU_output_alu
  DataMemory Data_Mem (
    .Address(ADDR), .Write_Data(Registers_rd_2), .Write(MW), .Read(not_1_out), .reset(1'b0),
    .Read_Data(Data_Mem_read_data));
  not not_1 (not_1_out, MW);
  Multiplexer #(.width(8)) multiplexer_1 (
    .in0(ALU_output_alu), .in1(Data_Mem_read_data), .out(multiplexer_1_out), .sel(RSource));  // open: en
  Registers Registers (
    .Input(multiplexer_1_out), .rd(RD), .rs(RS), .WR(RW), .rd_2(Registers_rd_2), .rs_2(Registers_rs_2));
  ALU ALU (.A(Registers_rs_2), .B(multiplexer_2_out), .Func(FUNC), .Output_ALU(ALU_output_alu));
  Multiplexer #(.width(8)) multiplexer_2 (
    .in0(Registers_rd_2), .in1(IMM), .out(multiplexer_2_out), .sel(IMTY));  // open: en
  // Probe on Registers_rs_2
  // Probe on Registers_rd_2
  Clock clock_1 (.out(CLK));
  Multiplexer multiplexer_3 (.in0(CLK), .in1(1'b0), .out(multiplexer_3_out), .sel(HALT));  // open: en
  InstrMemory Instr_Mem (.RESET(PC_____0), .out_2(Instr_Mem_out_2));
  Decoder Decoder (.\input (Instr_Mem_out_2), .opc(Decoder_opc), .rd(RD), .rs(RS), .addr(ADDR), .imm(IMM), .func(FUNC));
  Control_Unit Control_Unit (.opc(Decoder_opc), .RW(RW), .halt(HALT), .imty(IMTY), .MW(MW), .Rsource(RSource));
endmodule

module Control_Unit (
  input  [2:0] opc,
  output RW,
  output halt,
  output imty,
  output MW,
  output Rsource
);

  wire and_1_out, and_2_out, and_5_out, multiplexer_1_out, not_1_out, not_2_out, not_4_out, not_5_out;

  not not_1 (not_1_out, opc[2]);
  not not_2 (not_2_out, opc[2]);
  not not_3 (imty, opc[1]);
  not not_4 (not_4_out, opc[1]);
  not not_5 (not_5_out, opc[0]);
  and and_1 (and_1_out, not_1_out, opc[0]);
  and and_2 (and_2_out, not_2_out, opc[1]);
  and and_3 (MW, not_4_out, not_5_out);
  and and_4 (Rsource, opc[1], opc[0]);
  or or_1 (RW, and_1_out, and_2_out);
  and and_5 (and_5_out, RW, imty, MW);
  Multiplexer #(.enable("false")) multiplexer_1 (.in0(Rsource), .in1(and_5_out), .out(multiplexer_1_out), .sel(RW));
  Comparator #(.width(1)) comparator_1 (.a(multiplexer_1_out), .b(1'b1), .eq(halt));  // open: gt, lt

  // Notes on the sheet:
  //   -------> only operative when opc = 111
  //   Aka Instruction final
endmodule

module InstrMemory (
  input  RESET,
  output [15:0] out_2
);

  wire clock_1_out;
  wire [7:0] pc_q;

  Clock clock_1 (.out(clock_1_out));
  Counter pc (.Q(pc_q), .clk(clock_1_out), .clr(RESET));  // open: load, D, count, carry
  RAM #(.dataWidth(16)) ram_1 (.addr(pc_q), .data(out_2), .clk(clock_1_out), .ld(1'b1));  // open: sel, clr
endmodule

module DataMemory (
  input  [5:0] Address,
  input  [7:0] Write_Data,
  input  Write,
  input  Read,
  input  reset,
  output [7:0] Read_Data
);

  wire clock_1_out;

  Clock clock_1 (.out(clock_1_out));
  RAM #(.addrWidth(6), .bus("separate")) ram_1 (
    .addr(Address), .din(Write_Data), .data(Read_Data), .str(Write), .sel(1'b1), .clk(clock_1_out),
    .ld(Read), .clr(reset));
endmodule

module Registers (
  input  [7:0] Input,
  input  rd,
  input  rs,
  input  WR,
  output [7:0] rd_2,
  output [7:0] rs_2
);

  wire clock_1_out, demultiplexer_2_out0, demultiplexer_2_out1;
  wire [7:0] demultiplexer_1_out0, demultiplexer_1_out1, R0_q, R1_q;

  Demultiplexer #(.width(8)) demultiplexer_1 (
    .out0(demultiplexer_1_out0), .out1(demultiplexer_1_out1), .in(Input), .sel(rd));  // open: en
  Demultiplexer demultiplexer_2 (
    .out0(demultiplexer_2_out0), .out1(demultiplexer_2_out1), .in(WR), .sel(rd));  // open: en
  Clock clock_1 (.out(clock_1_out));
  Register R0 (.D(demultiplexer_1_out0), .en(demultiplexer_2_out0), .Q(R0_q), .clk(clock_1_out));  // open: clr
  Register R1 (.D(demultiplexer_1_out1), .en(demultiplexer_2_out1), .Q(R1_q), .clk(clock_1_out));  // open: clr
  Hex_Digit_Display hex_digit_display_1 (.value(rd_2[7:4]));  // open: dp
  Multiplexer #(.width(8)) multiplexer_1 (.in0(R0_q), .in1(R1_q), .out(rd_2), .sel(rd));  // open: en
  Multiplexer #(.width(8)) multiplexer_2 (.in0(R0_q), .in1(R1_q), .out(rs_2), .sel(rs));  // open: en
  Hex_Digit_Display hex_digit_display_2 (.value(rd_2[3:0]));  // open: dp
endmodule

module Decoder (
  input  [15:0] \input ,
  output [5:0] addr,
  output [7:0] imm,
  output [2:0] func,
  output rd,
  output rs,
  output [2:0] opc
);


  assign addr = \input [5:0];
  assign func = \input [10:8];
  assign imm = \input [7:0];
  assign opc = \input [15:13];
  assign rd = \input [12];
  assign rs = \input [11];
endmodule

module op2 (
  input  [7:0] A,
  input  [7:0] B,
  output [7:0] Out2
);

  Adder adder_1 (.a(A), .b(B), .out(Out2));  // open: cin, cout
endmodule

module op3 (
  input  [7:0] A,
  input  [7:0] B,
  output [7:0] Out3
);

  Subtractor subtractor_1 (.a(A), .b(B), .out(Out3));  // open: bin, bout
endmodule

module op4 (
  input  [7:0] A,
  input  [7:0] B,
  output [7:0] Out4
);

  Multiplier multiplier_1 (.a(A), .b(B), .out(Out4));  // open: cin, cout
endmodule

module op5 (
  input  [7:0] A,
  input  [7:0] B,
  output [7:0] Out5
);

  Divider divider_1 (.a(A), .b(B), .out(Out5));  // open: upper, rem
endmodule

module op6 (
  input  [7:0] A,
  input  [7:0] B,
  output [7:0] Out6
);

  Divider #(.width(7)) divider_1 (.a(A[6:0]), .b(B[6:0]), .rem(Out6[6:0]));  // open: out, upper
  xor xor_1 (Out6[7], A[7], B[7]);
endmodule

module op7 (
  input  [7:0] A,
  input  [7:0] B,
  output [7:0] Out7
);

  wire comparator_1_gt;

  Multiplexer #(.width(8), .enable("false")) multiplexer_1 (.in0(A), .in1(B), .out(Out7), .sel(comparator_1_gt));
  Comparator comparator_1 (.a(A), .b(B), .gt(comparator_1_gt));  // open: eq, lt
endmodule

module ALU (
  input  [7:0] A,
  input  [7:0] B,
  input  [2:0] Func,
  output [7:0] Output_ALU
);

  wire [7:0] op2_1_out2, op3_1_out3, op4_1_out4, op5_1_out5, op6_1_out6, op7_1_out7;

  op2 op2_1 (.A(A), .B(B), .Out2(op2_1_out2));
  op3 op3_1 (.A(A), .B(B), .Out3(op3_1_out3));
  op4 op4_1 (.A(A), .B(B), .Out4(op4_1_out4));
  op5 op5_1 (.A(A), .B(B), .Out5(op5_1_out5));
  op6 op6_1 (.A(A), .B(B), .Out6(op6_1_out6));
  op7 op7_1 (.A(A), .B(B), .Out7(op7_1_out7));
  Multiplexer #(.select(3), .width(8), .enable("false")) multiplexer_1 (
    .in0(A), .in1(B), .in2(op2_1_out2), .in3(op3_1_out3), .in4(op4_1_out4), .in5(op5_1_out5),
    .in6(op6_1_out6), .in7(op7_1_out7), .out(Output_ALU), .sel(Func));
endmodule
