// Logisim project Z23-AFEX.circ as structural Verilog: 13 circuits, main circuit Z23
module Z23 (
  input  PC_____0,
  output HALT
);

  wire CLK, IMTY, LI, multiplexer_5_out, MW, not_1_out, RD, RS, RSource, RW;
  wire [2:0] decoder_1_opc, FUNC;
  wire [5:0] ADDR, dir, multiplexer_1_out;
  wire [7:0] ALU_output_alu, Data_Mem_read_data, IMM, multiplexer_2_out, multiplexer_3_out,
       multiplexer_4_out, Registers_rd_2, Registers_rs_2;
  wire [15:0] Instr_Mem_instruction;

  Multiplexer #(.width(6)) multiplexer_1 (.in0(ADDR), .in1(dir), .out(multiplexer_1_out), .sel(LI));  // open: en
  // Probe on ALU_output_alu
  DataMemory Data_Mem (
    .Address(multiplexer_1_out), .Write_Data(multiplexer_3_out), .CLK(CLK), .Write(MW), .Read(not_1_out),
    .reset(1'b0), .Read_Data(Data_Mem_read_data));
  not not_1 (not_1_out, MW);
  Multiplexer #(.width(8)) multiplexer_2 (
    .in0(ALU_output_alu), .in1(Data_Mem_read_data), .out(multiplexer_2_out), .sel(RSource));  // open: en
  Registers Registers (
    .Input(multiplexer_2_out), .rd(RD), .rs(RS), .WR(RW), .CLK(CLK), .rd_2(Registers_rd_2),
    .rs_2(Registers_rs_2));
  ALU ALU (.A(Registers_rs_2), .B(multiplexer_4_out), .Func(FUNC), .Output_ALU(ALU_output_alu));
  Multiplexer #(.width(8)) multiplexer_3 (
    .in0(Registers_rd_2), .in1(IMM), .out(multiplexer_3_out), .sel(LI));  // open: en
  Multiplexer #(.width(8)) multiplexer_4 (
    .in0(Registers_rd_2), .in1(IMM), .out(multiplexer_4_out), .sel(IMTY));  // open: en
  // Probe on Registers_rs_2
  // Probe on Registers_rd_2
  Clock clock_1 (.out(CLK));
  Multiplexer multiplexer_5 (.in0(CLK), .in1(1'b0), .out(multiplexer_5_out), .sel(HALT));  // open: en
  InstrMemory Instr_Mem (.clock(multiplexer_5_out), .RESET(PC_____0), .Instruction(Instr_Mem_instruction));
  Decoder decoder_1 (
    .\input (Instr_Mem_instruction), .opc(decoder_1_opc), .rd(RD), .rs(RS), .addr(ADDR), .imm(IMM),
    .func(FUNC), .dir(dir));
  Control_Unit Control_Unit (
    .opc(decoder_1_opc), .RW(RW), .halt(HALT), .imty(IMTY), .MW(MW), .Rsource(RSource), .LI(LI));
endmodule

module Control_Unit (
  input  [2:0] opc,
  output RW,
  output halt,
  output imty,
  output MW,
  output Rsource,
  output LI
);

  wire and_1_out, and_2_out, and_5_out, and_7_out, multiplexer_1_out, nand_1_out, not_1_out, not_2_out,
       not_4_out, not_5_out, not_6_out;

  not not_1 (not_1_out, opc[2]);
  not not_2 (not_2_out, opc[2]);
  not not_3 (imty, opc[1]);
  not not_4 (not_4_out, opc[1]);
  not not_5 (not_5_out, opc[0]);
  not not_6 (not_6_out, opc[1]);
  nand nand_1 (nand_1_out, opc[2], opc[1]);
  and and_1 (and_1_out, not_1_out, opc[0]);
  and and_2 (and_2_out, not_2_out, opc[1]);
  and and_3 (MW, not_4_out, not_5_out);
  and and_4 (Rsource, opc[1], opc[0]);
  and and_5 (and_5_out, not_6_out, opc[2]);
  or or_1 (RW, and_1_out, and_2_out);
  and and_6 (LI, and_5_out, nand_1_out);
  and and_7 (and_7_out, RW, imty, MW);
  Multiplexer #(.enable("false")) multiplexer_1 (.in0(Rsource), .in1(and_7_out), .out(multiplexer_1_out), .sel(RW));
  Comparator #(.width(1)) comparator_1 (.a(multiplexer_1_out), .b(1'b1), .eq(halt));  // open: gt, lt

  // Notes on the sheet:
  //   -------> only operative when opc = 111
  //   Aka Instruction final
endmodule

module InstrMemory (
  input  clock,
  input  RESET,
  output [15:0] Instruction
);

  wire [7:0] adder_1_out, PC_q;

  Register PC (.D(adder_1_out), .Q(PC_q), .clk(clock), .clr(RESET));  // open: en
  Adder adder_1 (.a(8'h1), .b(PC_q), .out(adder_1_out));  // open: cin, cout
  RAM #(.dataWidth(16)) ram_1 (.addr(PC_q), .data(Instruction), .clk(clock), .ld(1'b1));  // open: sel, clr
endmodule

module DataMemory (
  input  [5:0] Address,
  input  [7:0] Write_Data,
  input  Write,
  input  Read,
  input  reset,
  input  CLK,
  output [7:0] Read_Data
);

  RAM #(.addrWidth(6), .bus("separate")) ram_1 (
    .addr(Address), .din(Write_Data), .data(Read_Data), .str(Write), .sel(1'b1), .clk(CLK), .ld(Read),
    .clr(reset));
endmodule

module Registers (
  input  [7:0] Input,
  input  rd,
  input  rs,
  input  WR,
  input  CLK,
  output [7:0] rd_2,
  output [7:0] rs_2
);

  wire demultiplexer_2_out0, demultiplexer_2_out1;
  wire [7:0] demultiplexer_1_out0, demultiplexer_1_out1, R0_q, R1_q;

  Demultiplexer #(.width(8)) demultiplexer_1 (
    .out0(demultiplexer_1_out0), .out1(demultiplexer_1_out1), .in(Input), .sel(rd));  // open: en
  Demultiplexer demultiplexer_2 (
    .out0(demultiplexer_2_out0), .out1(demultiplexer_2_out1), .in(WR), .sel(rd));  // open: en
  Register R0 (.D(demultiplexer_1_out0), .en(demultiplexer_2_out0), .Q(R0_q), .clk(CLK));  // open: clr
  Register R1 (.D(demultiplexer_1_out1), .en(demultiplexer_2_out1), .Q(R1_q), .clk(CLK));  // open: clr
  Hex_Digit_Display hex_digit_display_1 (.value(rd_2[7:4]));  // open: dp
  Multiplexer #(.width(8)) multiplexer_1 (.in0(R0_q), .in1(R1_q), .out(rd_2), .sel(rd));  // open: en
  Multiplexer #(.width(8)) multiplexer_2 (.in0(R0_q), .in1(R1_q), .out(rs_2), .sel(rs));  // open: en
  Hex_Digit_Display hex_digit_display_2 (.value(rd_2[3:0]));  // open: dp
  Hex_Digit_Display hex_digit_display_3 (.value(rs_2[3:0]));  // open: dp
  Hex_Digit_Display hex_digit_display_4 (.value(rs_2[7:4]));  // open: dp
endmodule

module Decoder (
  input  [15:0] \input ,
  output [5:0] addr,
  output [7:0] imm,
  output [2:0] func,
  output rd,
  output rs,
  output [2:0] opc,
  output [5:0] dir
);


  assign addr = \input [5:0];
  assign dir = \input [13:8];
  assign func = \input [10:8];
  assign imm = \input [7:0];
  assign opc = \input [15:13];
  assign rd = \input [12];
  assign rs = \input [11];
endmodule

module op2 (
  input  [7:0] A,
  input  [7:0] B,
  output [7:0] Out2
);

  Adder adder_1 (.a(A), .b(B), .out(Out2));  // open: cin, cout
endmodule

module op3 (
  input  [7:0] A,
  input  [7:0] B,
  output [7:0] Out3
);

  Subtractor subtractor_1 (.a(A), .b(B), .out(Out3));  // open: bin, bout
endmodule

module op4 (
  input  [7:0] A,
  input  [7:0] B,
  output [7:0] Out4
);

  Multiplier multiplier_1 (.a(A), .b(B), .out(Out4));  // open: cin, cout
endmodule

module op5 (
  input  [7:0] A,
  input  [7:0] B,
  output [7:0] Out5
);

  Divider #(.width(7)) divider_1 (.a(A[6:0]), .b(B[6:0]), .out(Out5[6:0]));  // open: upper, rem
  xor xor_1 (Out5[7], A[7], B[7]);
endmodule

module op6 (
  input  [7:0] A,
  input  [7:0] B,
  output [7:0] Out6
);

  Divider #(.width(7)) divider_1 (.a(A[6:0]), .b(B[6:0]), .rem(Out6[6:0]));  // open: out, upper
  xor xor_1 (Out6[7], A[7], B[7]);
endmodule

module op7 (
  input  [7:0] A,
  input  [7:0] B,
  output [7:0] Out7
);

  wire comparator_1_gt;

  Multiplexer #(.width(8), .enable("false")) multiplexer_1 (.in0(A), .in1(B), .out(Out7), .sel(comparator_1_gt));
  Comparator comparator_1 (.a(A), .b(B), .gt(comparator_1_gt));  // open: eq, lt
endmodule

module ALU (
  input  [7:0] A,
  input  [7:0] B,
  input  [2:0] Func,
  output [7:0] Output_ALU
);

  wire [7:0] op2_1_out2, op3_1_out3, op4_1_out4, op5_1_out5, op6_1_out6, op7_1_out7;

  op2 op2_1 (.A(A), .B(B), .Out2(op2_1_out2));
  op3 op3_1 (.A(A), .B(B), .Out3(op3_1_out3));
  op4 op4_1 (.A(A), .B(B), .Out4(op4_1_out4));
  op5 op5_1 (.A(A), .B(B), .Out5(op5_1_out5));
  op6 op6_1 (.A(A), .B(B), .Out6(op6_1_out6));
  op7 op7_1 (.A(A), .B(B), .Out7(op7_1_out7));
  Multiplexer #(.select(3), .width(8), .enable("false")) multiplexer_1 (
    .in0(A), .in1(B), .in2(op2_1_out2), .in3(op3_1_out3), .in4(op4_1_out4), .in5(op5_1_out5),
    .in6(op6_1_out6), .in7(op7_1_out7), .out(Output_ALU), .sel(Func));
endmodule
