// Logisim project adder.circ as structural Verilog: 1 circuit, main circuit main
module main (
  input  A,
  input  B
);

  wire adder_1_cout, adder_1_out, and_1_out, comparator_1_gt, multiplexer_1_out, multiplexer_2_out,
       multiplexer_3_out, subtractor_1_out, xor_1_out;

  Adder #(.width(1)) adder_1 (.a(A), .b(B), .out(adder_1_out), .cout(adder_1_cout));  // open: cin
  Multiplexer #(.enable("false")) multiplexer_1 (.in0(B), .in1(A), .out(multiplexer_1_out), .sel(comparator_1_gt));
  Multiplexer #(.enable("false")) multiplexer_2 (.in0(B), .in1(A), .out(multiplexer_2_out), .sel(comparator_1_gt));
  Comparator #(.width(1)) comparator_1 (.a(A), .b(B), .gt(comparator_1_gt));  // open: eq, lt
  xor xor_1 (xor_1_out, A, B);
  Multiplexer #(.enable("false")) multiplexer_3 (.in0(B), .in1(A), .out(multiplexer_3_out), .sel(comparator_1_gt));
  Subtractor #(.width(1)) subtractor_1 (
    .a(multiplexer_1_out), .b(multiplexer_2_out), .out(subtractor_1_out));  // open: bin, bout
  Multiplexer #(.enable("false")) multiplexer_4 (
    .in0(adder_1_out), .in1(subtractor_1_out), .out(multiplexer_3_out), .sel(xor_1_out));
  and and_1 (and_1_out, adder_1_cout, ~xor_1_out);  // AND_Gate
  // Probe on multiplexer_3_out
endmodule
