// Logisim project corbera_1_Basic.circ as structural Verilog: 2 circuits, main circuit main
module main (
  input  [7:0] A,
  input  [7:0] B,
  input  in_3,
  output [7:0] OUT,
  output zero,
  output negative
);

  choser choser_1 (.A(A), .B(B), .sum_sub(in_3), .out(OUT), .out_5(zero), .NEGATIVE(negative));
endmodule

// CHOSER
module choser (
  input  [7:0] A,
  input  [7:0] B,
  input  sum_sub,
  output [7:0] out,
  output out_5,
  output NEGATIVE
);

  wire [7:0] adder_1_out, subtractor_1_out;

  Adder adder_1 (.a(A), .b(B), .out(adder_1_out));  // open: cin, cout
  Subtractor subtractor_1 (.a(A), .b(B), .out(subtractor_1_out));  // open: bin, bout
  Multiplexer #(.width(8), .enable("false")) multiplexer_1 (
    .in0(adder_1_out), .in1(subtractor_1_out), .out({NEGATIVE, out[6:0]}), .sel(sum_sub));
  nor nor_1 (out_5, out[0], out[1], out[2], out[3], out[5], out[6], NEGATIVE, out[4]);

  assign out[7] = NEGATIVE;

  // Other names for the same wires on the sheet: _5th = out[4]; tun = sum_sub
endmodule
