// Logisim project muxvsdemus.circ as structural Verilog: 1 circuit, main circuit main
module main (
  input  [1:0] in_1,
  input  [1:0] output_location_choser,
  input  [1:0] in_3,
  input  [1:0] in_4,
  input  [1:0] in_5,
  input  [1:0] in_6,
  input  [1:0] input_choser,
  output [1:0] out_8,
  output [1:0] out_9,
  output [1:0] out_10,
  output [1:0] out_11,
  output [1:0] out_12
);

  Demultiplexer #(.select(2), .width(2), .enable("false")) demultiplexer_1 (
    .out0(out_8), .out1(out_9), .out2(out_10), .out3(out_11), .in(in_1), .sel(output_location_choser));
  Multiplexer #(.select(2), .width(2), .enable("false")) multiplexer_1 (
    .in0(in_3), .in1(in_4), .in2(in_5), .in3(in_6), .out(out_12), .sel(input_choser));

  // Notes on the sheet:
  //   the de-mux given a number and an output to copy in, it does
  //   the mux given 4 chooses by an input one of the four inputs to copy
endmodule
